# Fritzing sketch example (saved by Fritzing 0.8.7b)
breadboards: 1

parts:
  Part1 = Arduino Uno (Rev3)
  LED1 = LED - 5mm [color="Green (555nm)" package="5 mm [THT]"]
  LED2 = LED - 5mm [color="Yellow (595nm)" package="5 mm [THT]"]
  LED3 = LED - 5mm [color="Red (633nm)" package="5 mm [THT]"]

nets:
  N1: Part1.D9_PWM, LED3.cathode
  N2: Part1.D11_PWM/MOSI, LED2.cathode
  N3: Part1.D13/SCK, LED1.cathode
  N4: Part1.GND, LED1.anode, LED2.anode, LED3.anode
